# Fritzing sketch board (saved by Fritzing 0.9.4)
breadboards: 1

parts:
  LED1 = RGB LED (com. anode, rbg) [package="5 mm [THT]"]
  Part1 = Arduino Uno (Rev3)
  Part2 = Thumb Joystick
  R1 = Resistor [tolerance=±5% resistance=220 package="0603 [SMD]"]
  R2 = Resistor [tolerance=±5% resistance=220 package="0603 [SMD]"]
  R3 = Resistor [tolerance=±5% resistance=220 package="0603 [SMD]"]

nets:
  N1: LED1.red_cathode, R1.Pin_0
  GND: LED1.common_anode, Part1.GND, Part2.GND
  N2: LED1.blue_cathode, R2.Pin_0
  N3: LED1.green_cathode, R3.Pin_0
  N4: Part1.A0, Part2.HORZ
  N5: Part1.A1, Part2.VERT
  N6: Part1.D2, Part2.VCC
  N7: Part1.D3_PWM, R3.Pin_1
  N8: Part1.D5_PWM, R2.Pin_1
  N9: Part1.D6_PWM, R1.Pin_1
  N10: Part1.5V, Part2.SEL
